# Fritzing sketch IoT (saved by Fritzing 0.9.3b)
breadboards: 1

parts:
  Part7 = KY-015 Temperature & Humidity Sensor Module [package="Breakout board"]
  R3 = PHOTOCELL [package=photocell]
  Mod2 = Raspberry Pi Pico W
  WATER_PUMP2 = water pump/motor
  Part8 = FC-28 Soil Hygrometer Module
  Part9 = FC-28 Soil Hygrometer Module
  Part10 = FC-28 Soil Hygrometer Module - Probe
  Part11 = FC-28 Soil Hygrometer Module - Probe
  SERVO2 = Tower Pro SG90 servo [part_number=101246]
  Part12 = KY-019 5V Relay Module [package="Breakout board"]
  R4 = Resistor [tolerance=±5% resistance=220 package=THT]
  LED3 = LED - 5mm [color="Red (633nm)" package="5 mm [THT]"]
  HC-SR04_Sensor_2 = HC-SR04 Ultrasonic Distance Sensor
  VCC1 = 4 x AA Battery Box

nets:
  N1: Part7.S, Mod2.pin_15
  VIN: Part7.Vin, SERVO2.+5V, Part12.+, HC-SR04_Sensor_2.VCC
  GND: Part7.-, Mod2.pin_3, Mod2.pin_8, Mod2.pin_13, Mod2.pin_18, Mod2.pin_23, Mod2.pin_28, Mod2.pin_33, Mod2.pin_38, Mod2.pin_42, SERVO2.GND, LED3.cathode, HC-SR04_Sensor_2.GND
  N2: R3.P$1, Mod2.pin_36
  N3: R3.P$2, Mod2.pin_31, R4.Pin_0
  N4: Mod2.pin_1, SERVO2.Signal
  N5: Mod2.pin_14, LED3.anode
  N6: Mod2.pin_16, HC-SR04_Sensor_2.TRIG
  N7: Mod2.pin_17, HC-SR04_Sensor_2.ECHO
  VCC: Mod2.pin_20, Part8.VCC, Part9.VCC
  N8: Mod2.pin_27, Part12.S
  N9: Mod2.pin_32, Part8.AO
  N10: Mod2.pin_34, Part9.AO
  N11: WATER_PUMP2.pin_1, VCC1.-
  N12: WATER_PUMP2.pin_2, Part12.NO
  GND_2: Part8.GND, Part9.GND, Part12.-, R4.Pin_1
  N13: Part8.POS, Part11.POS
  N14: Part8.NEG, Part11.NEG
  N15: Part9.POS, Part10.POS
  N16: Part9.NEG, Part10.NEG
  N17: Part12.Common, VCC1.+

notes:
  Water Pump
  Photoresistor
  Soil Moisture Sensor
  Relay
  Ultrasonic Distance Sensor
  DHT11 Sensor
  Micro servo TS90 / SG90 1.2 kg

custom parts:
  KY-015 Temperature & Humidity Sensor Module: DH-11 temperature and humidity sensor in KEYES KY-015 module, provides a low-latency serial interface to measure humidity and temperature.
  Raspberry Pi Pico W: Raspberry Pi Pico W. Based around the RP2040 microcontroller the Pico W is a low cost microcontroller device bringing Raspberry Pi quality, cost, and easy of use to the microcontroller space. The areas marked KEEPOUT in pcb silkscreen should not have traces running through them to avoid shorts on a soldered in module!
  water pump/motor: WATER PUMP BY ARDUBLOCKTR
  FC-28 Soil Hygrometer Module: The FC-28 is a soil hygrometer module that uses the Texas Instruments LM393 comparator chip to provide an analog measurement of soil humidity. The digital output is high when soil moisture is over a certain threshold, as determined by adjusting the potentiometer.
  FC-28 Soil Hygrometer Module - Probe: The FC-28 is a soil hygrometer module that uses the Texas Instruments LM393 comparator chip to provide an analog measurement of soil humidity.
  Tower Pro SG90 servo: Original file by John De Cristofaro http://www.adafruit.com/products/1449 Adafruit Feedback Servo (Small) Edited by: e-radionica.com 28/9/2015
  KY-019 5V Relay Module: 5V Relay module KEYES KY-019, used to control AC circuits.
  4 x AA Battery Box: A 4 x AA battery box.
